// Logisim project t888.circ as structural Verilog: 3 circuits, main circuit t888
module t888 (
  input  [7:0] in_1,
  input  [7:0] in_2,
  input  in_3,
  input  in_4,
  input  in_5,
  input  in_6
);

  wire undriven;

  ALU alu_1 ();  // open: DataBus, Command, State, DataBus_2, clr, clk
  // Probe on in_2
  RAM #(.Select("low")) ram_1 (.addr(in_1), .data(in_2), .sel(undriven), .clk(in_4), .ld(in_5), .clr(in_6));
endmodule

module ALU (
  input  [7:0] DataBus,
  input  [7:0] Command,
  input  clk,
  input  clr,
  output [1:0] State,
  output [7:0] DataBus_2
);

  wire adder_2_cout, C_en_q, multiplexer_1_out, nor_1_out, not_2_out, subtractor_2_bout, subtractor_3_bout,
       zerotest_1_iszero;
  wire [1:0] controlled_buffer_2_out;
  wire [7:0] Accum_q, adder_1_out, adder_2_out, and_2_out, Data_q, multiplexer_2_out, negator_1_out,
       not_1_out, or_1_out, subtractor_1_out, subtractor_2_out, subtractor_3_out, xor_1_out;
  wire [7:7] and_1_out;

  Register #(.trigger("low"), .Select("low")) Data (.D(DataBus), .Q(Data_q), .clk(clk));  // open: en, clr
  Register #(.Select("low")) Accum (
    .D(multiplexer_2_out), .en(controlled_buffer_2_out[0]), .Q(Accum_q), .clk(clk), .clr(clr));
  assign DataBus_2 = controlled_buffer_2_out[1] ? multiplexer_2_out : 8'bz;  // Controlled_Buffer controlled_buffer_1
  assign controlled_buffer_2_out = ~clk ? Command[7:6] : 2'bz;  // Controlled_Buffer controlled_buffer_2
  and and_1 (and_1_out[7], C_en_q, State[1]);
  assign not_1_out = ~Accum_q;  // NOT_Gate not_1, 8 bits wide
  Negator negator_1 (.in(Accum_q), .out(negator_1_out));
  Subtractor subtractor_1 (.a(Accum_q), .b(8'h1), .out(subtractor_1_out));  // open: bin, bout
  Adder adder_1 (.a(Accum_q), .b(8'h1), .out(adder_1_out));  // open: cin, cout
  assign xor_1_out = Accum_q ^ Data_q;  // XOR_Gate xor_1, 8 bits wide
  assign or_1_out = Accum_q | Data_q;  // OR_Gate or_1, 8 bits wide
  assign and_2_out = Accum_q & Data_q;  // AND_Gate and_2, 8 bits wide
  Subtractor subtractor_2 (
    .a(Data_q), .b(Accum_q), .out(subtractor_2_out), .bin(and_1_out[7]), .bout(subtractor_2_bout));
  Subtractor subtractor_3 (
    .a(Accum_q), .b(Data_q), .out(subtractor_3_out), .bin(and_1_out[7]), .bout(subtractor_3_bout));
  Adder adder_2 (.a(Accum_q), .b(Data_q), .out(adder_2_out), .cin(and_1_out[7]), .cout(adder_2_cout));
  not not_2 (not_2_out, Command[4]);
  Register #(.width(1), .Select("high")) C_en (.D(Command[1]), .en(Command[0]), .Q(C_en_q), .clk(clk), .clr(clr));
  Multiplexer #(.select(3)) multiplexer_1 (
    .in1(adder_2_cout), .in2(subtractor_3_bout), .in3(subtractor_2_bout), .in5(Accum_q[7]), .in6(Accum_q[0]),
    .in7(Accum_q[0]), .out(multiplexer_1_out), .sel({Command[5], Command[3:2]}), .en(not_2_out));  // open: in0, in4
  Register #(.width(1), .Select("high")) Carry (
    .D(multiplexer_1_out), .Q(State[1]), .clk(clk), .clr(Command[0]));  // open: en
  Multiplexer #(.select(4), .width(8), .enable("false")) multiplexer_2 (
    .in0(Data_q), .in1(adder_2_out), .in2(subtractor_3_out), .in3(subtractor_2_out), .in4(and_2_out),
    .in5(or_1_out), .in6(xor_1_out), .in7(Accum_q), .in8({Accum_q[6:0], and_1_out[7]}),
    .in9({and_1_out[7], Accum_q[7:1]}), .in10({{2{Accum_q[7]}}, Accum_q[6:1]}), .in11(adder_1_out),
    .in12(subtractor_1_out), .in13(negator_1_out), .in14(not_1_out), .in15({8{1'b0}}),
    .out(multiplexer_2_out), .sel(Command[5:2]));
  ZeroTest zerotest_1 (.Input(multiplexer_2_out), .IsZero(zerotest_1_iszero));
  Register #(.width(1), .Select("high")) Zero (
    .D(zerotest_1_iszero), .en(nor_1_out), .Q(State[0]), .clk(clk), .clr(clr));
  nor nor_1 (nor_1_out, Command[2], Command[3], Command[4]);

  // Notes on the sheet:
  //   DataBus: pull=down
  //   Command: pull=down
endmodule

module ZeroTest (
  input  [7:0] Input,
  output IsZero
);

  nor nor_1 (IsZero, Input[0], Input[1], Input[2], Input[3], Input[4], Input[5], Input[6], Input[7]);

  // Notes on the sheet:
  //   Input: pull=up
endmodule
